# Fritzing sketch interrupt (saved by Fritzing 0.9.4)
breadboards: 1

parts:
  S1 = Momentary Switch [package=ksa_sealed_tac_switch]
  Part1 = Arduino Uno (Rev3)

nets:
  N1: S1.1, Part1.5V
  N2: S1.3, Part1.D2
  N3: S1.4, Part1.GND
